# Fritzing sketch Door Pi (saved by Fritzing 0.9.4)
circuit board: 8.53488cm x 5.63626cm
breadboards: 1

parts:
  J6 = Camdenboss CTB0158-8 [part_number=CTB0158-8 package=THT]
  GV5-1 = Omron_MY2K_02_12VDC_3A [part_number=GV5-2 package=THT]
  12V = 2.1mm DC Barrel Jack
  LLC1 = Logic Level Converter [package="Breakout board"]
  GV5-2 = Omron_MY2K_02_12VDC_3A [part_number=GV5-2 package=THT]
  DoorBell = Camdenboss CTB0158-2 [part_number=CTB0158-2 package=THT]
  DoorStrike = Camdenboss CTB0158-2 [part_number=CTB0158-2 package=THT]
  U1 = TSR12450
  5V_LED = LEDs [package=led10mm]
  3_3V_LED = LEDs [package=led10mm]
  12V_LED = LEDs [package=led10mm]
  R1 = Resistor [tolerance=±5% resistance=220 package=THT]
  J10 = Raspberry Pi Header 40pin [package=THT]

nets:
  N1: J6.pin1, GV5-1.GND/Vcc, 12V.center_(V+), GV5-2.GND/Vcc, U1.IN, 12V_LED.A
  GND: J6.pin2, GV5-1.Set/Reset#90, 12V.GND, LLC1.L-GND, LLC1.H-GND, GV5-2.Set/Reset#90, DoorBell.pin1, DoorStrike.pin1, U1.GND, 5V_LED.C, 12V_LED.C, J10.GND
  N2: J6.pin3, LLC1.HV1
  N3: J6.pin4, LLC1.HV2
  N4: J6.pin5, R1.Pin_1
  N5: GV5-1.Out_1-1, DoorBell.pin2
  N6: GV5-1.Set/Reset#89, J10.IO4
  N7: LLC1.LV1, J10.IO14
  N8: LLC1.LV2, J10.IO15
  N9: LLC1.LV, 3_3V_LED.A, J10.3V3
  N10: LLC1.HV, U1.OUT, 5V_LED.A, J10.5V
  N11: GV5-2.Out_1-1, DoorStrike.pin2
  N12: GV5-2.Set/Reset#89, J10.IO17
  N13: R1.Pin_0, J10.IO5

custom parts:
  Omron_MY2K_02_12VDC_3A: Omron GV5-2, 12VDC @ 2 Amp, Bistable, Low Signal Relay, DPDT, No Coil Polarity
  2.1mm DC Barrel Jack: 2.1mm DC Barrel Jack with Thru-Hole Connectors (breadboardable)
  Logic Level Converter: 5V to/from 3.3V logic level converter
  TSR12450: Mini DC/DC Step-Down (Buck) Converter - 5V @ 1A output - TSR12450
  Raspberry Pi Header 40pin: Raspberry Pi 40 pin header - for creating your own shields. (Mar 2020, bb: make breadboard friendly (.4in pin spacing) and add labels. Schematic add labels. PCB make oblong pins to allow routing traces between the pins.)
